// Digital circuit MicroMachine.dig as structural Verilog
module MicroMachine (
  input  init,
  input  clk
);

  wire _1WordInstr, and_1_out, and_2_out, and_3_out, and_4_out, arg1S, ARG2S, arg2S_t, ceFlags, ceInstr,
       cePC, ceRegA, ceRegB, cstFetch_t, destS, DoJR, IncrPC, incrPC_t, instrADD, instrALU, instrAND,
       instrCMP, InstrDecode, instrJA, instrLSR, instrMemRead, instrMemWrite, instrOR, instrPASS1,
       instrPASS2, instrSUB, instrXOR, JumpCondTrue, not_1_out, or_2_out, or_4_out, or_5_out, progFetch;
  wire [2:0] alu_1_p6, ZCN;
  wire [3:0] codeOp, counter_1_out, counter_1_out_2;
  wire [7:0] add_1_s, alu_1_p5, CST, MA, MDI, MDO, multiplexer_2_out, multiplexer_3_out, multiplexer_5_out,
       multiplexer_7_out, PC, Reg_A, Reg_B;
  wire [7:7] instr;

  not not_1 (not_1_out, instr[7]);
  Demultiplexer #(.Selector_Bits(4)) demultiplexer_1 (
    .sel({codeOp[3:2], ARG2S, codeOp[0]}), .in(not_1_out), .out_0(instrADD), .out_1(instrSUB),
    .out_2(instrAND), .out_3(instrOR), .out_4(instrXOR), .out_5(instrLSR), .out_6(instrCMP),
    .out_8(instrPASS1), .out_9(instrPASS2), .out_13(instrMemRead), .out_14(instrMemWrite), .out_15(instrJA));  // open: out_7, out_10, out_11, out_12
  or or_1 (instrALU, instrADD, instrSUB, instrAND, instrOR, instrXOR, instrLSR, instrCMP, instrPASS1, instrPASS2);
  or or_2 (or_2_out, instrALU, instrMemRead, instrMemWrite);
  Multiplexer #(.Selector_Bits(2)) multiplexer_1 (
    .sel(codeOp[3:2]), .in_0(1'b1), .in_1(ZCN[0]), .in_2(ZCN[1]), .in_3(ZCN[2]), .out(JumpCondTrue));
  and and_1 (and_1_out, or_2_out, ~arg2S_t);  // And
  or or_3 (_1WordInstr, instrPASS1, instr[7], and_1_out);
  and and_2 (and_2_out, InstrDecode, ~instr[7]);  // And
  or or_4 (or_4_out, ceFlags, DoJR);
  or or_5 (or_5_out, and_2_out, cstFetch_t);
  and and_3 (and_3_out, instr[7], InstrDecode);
  and and_4 (and_4_out, InstrDecode, ARG2S, ~instr[7]);  // And
  D_FF_AS InstrFetch (.Set(init), .D(or_4_out), .C(clk), .Clr(1'b0), .Q(ceInstr));  // open: nQ
  D_FF_AS u_InstrDecode (.Set(1'b0), .D(ceInstr), .C(clk), .Clr(init), .Q(InstrDecode));  // open: nQ
  D_FF_AS RegWrite (.Set(1'b0), .D(or_5_out), .C(clk), .Clr(init), .Q(ceFlags));  // open: nQ
  D_FF_AS u_DoJR (.Set(1'b0), .D(and_3_out), .C(clk), .Clr(init), .Q(DoJR));  // open: nQ
  D_FF_AS u_IncrPC (.Set(1'b0), .D(and_4_out), .C(clk), .Clr(init), .Q(incrPC_t));  // open: nQ
  D_FF_AS CstFetch (.Set(1'b0), .D(incrPC_t), .C(clk), .Clr(init), .Q(cstFetch_t));  // open: nQ
  or or_6 (cePC, ceFlags, cstFetch_t, DoJR);
  or or_7 (progFetch, ceInstr, 1'b0);
  and and_5 (ceRegA, ~destS, ceFlags);  // And
  and and_6 (ceRegB, destS, ceFlags);
  // Reg RegIR: pin names not known; wires that end beside it: MDI, ceInstr, init, clk, {instr[7], codeOp[3:2], ARG2S, codeOp[0], arg2S_t, arg1S, destS}
  Multiplexer #(.Bits(8)) multiplexer_2 (
    .sel(DoJR), .in_0(8'h1), .in_1({{4{ARG2S}}, codeOp[0], arg2S_t, arg1S, destS}), .out(multiplexer_2_out));
  Seven_Seg_Hex seven_seg_hex_1 (.d(MA[7:4]), .dp(1'b1));
  LED led_1 (.in(ceInstr));
  Seven_Seg_Hex seven_seg_hex_2 (.d(MA[3:0]), .dp(1'b1));
  LED led_2 (.in(InstrDecode));
  LED led_3 (.in(IncrPC));
  // Reg RegCst: pin names not known; wires that end beside it: MDI, 1'b0, init, clk, CST
  Add #(.Bits(8)) add_1 (.a(multiplexer_2_out), .b(PC), .c_i(1'b0), .s(add_1_s));  // open: c_o
  LED led_4 (.in(1'b0));
  LED led_5 (.in(1'b0));
  Seven_Seg_Hex seven_seg_hex_3 (.d(MDO[7:4]), .dp(1'b1));
  LED led_6 (.in(ceFlags));
  LED led_7 (.in(1'b0));
  Multiplexer #(.Bits(8)) multiplexer_3 (.sel(1'b0), .in_0(add_1_s), .in_1(CST), .out(multiplexer_3_out));
  Seven_Seg_Hex seven_seg_hex_4 (.d(MDO[3:0]), .dp(1'b1));
  LED led_8 (.in(1'b0));
  LED led_9 (.in(1'b0));
  // Reg PC: pin names not known; wires that end beside it: multiplexer_3_out, cePC, init, clk, PC
  Seven_Seg_Hex seven_seg_hex_5 (.d(MDI[7:4]), .dp(1'b1));
  LED led_10 (.in(1'b0));
  LED led_11 (.in(1'b0));
  Seven_Seg_Hex seven_seg_hex_6 (.d(MDI[3:0]), .dp(1'b1));
  Seven_Seg_Hex seven_seg_hex_7 (.d(PC[7:4]), .dp(1'b1));
  Seven_Seg_Hex seven_seg_hex_8 (.d(PC[3:0]), .dp(1'b1));
  LED N (.in(ZCN[0]));
  LED C (.in(ZCN[1]));
  LED N_2 (.in(ZCN[2]));
  Multiplexer #(.Bits(8)) multiplexer_4 (.sel(arg1S), .in_0(Reg_A), .in_1(Reg_B), .out(MDO));
  Multiplexer #(.Bits(8)) multiplexer_5 (.sel(arg2S_t), .in_0(Reg_A), .in_1(CST), .out(multiplexer_5_out));
  Seven_Seg_Hex seven_seg_hex_9 (.d({instr[7], codeOp[3:2], ARG2S}), .dp(1'b1));
  Seven_Seg_Hex seven_seg_hex_10 (.d({codeOp[0], arg2S_t, arg1S, destS}), .dp(1'b1));
  // ALU alu_1: pin names not known; wires that end beside it: MDO, multiplexer_5_out, arg2S_t, {codeOp[3:2], ARG2S, codeOp[0]}, alu_1_p5, alu_1_p6
  Multiplexer #(.Bits(8)) multiplexer_6 (.sel(progFetch), .in_0(multiplexer_5_out), .in_1(PC), .out(MA));
  Seven_Seg_Hex seven_seg_hex_11 (.d(CST[7:4]), .dp(1'b1));
  Seven_Seg_Hex seven_seg_hex_12 (.d(CST[3:0]), .dp(1'b1));
  Multiplexer #(.Bits(8)) multiplexer_7 (.sel(1'b0), .in_0(alu_1_p5), .in_1(MDI), .out(multiplexer_7_out));
  Register #(.Bits(3)) RegFlags (.D(alu_1_p6), .C(clk), .en(ceFlags), .Q(ZCN));
  Seven_Seg_Hex seven_seg_hex_13 (.d(Reg_A[7:4]), .dp(1'b1));
  // Reg Reg_A: pin names not known; wires that end beside it: multiplexer_7_out, ceRegA, init, clk, Reg_A
  // Reg Reg_B: pin names not known; wires that end beside it: multiplexer_7_out, ceRegB, init, clk, Reg_B
  Seven_Seg_Hex seven_seg_hex_14 (.d(Reg_A[3:0]), .dp(1'b1));
  Seven_Seg_Hex seven_seg_hex_15 (.d(Reg_B[7:4]), .dp(1'b1));
  Seven_Seg_Hex seven_seg_hex_16 (.d(Reg_B[3:0]), .dp(1'b1));
  Seven_Seg_Hex seven_seg_hex_17 (.d(counter_1_out_2), .dp(1'b1));
  Seven_Seg_Hex seven_seg_hex_18 (.d(counter_1_out), .dp(1'b1));
  Counter #(.Bits(8)) counter_1 (.en(1'b1), .C(clk), .clr(init), .out({counter_1_out_2, counter_1_out}));  // open: ovf
  EEPROMDualPort #(.AddrBits(8), .Bits(8)) eepromdualport_1 (
    .A(MA), .Din(MDO), .str(1'b0), .C(clk), .ld(1'b1), .D(MDI));

  // Other names for the same wires on the sheet: RegWrite = ceFlags; InstrFetch = ceInstr;
  //   instr[6:0] = {codeOp[3:2], ARG2S, codeOp[0], arg2S_t, arg1S, destS};
  //   offset[7:0] = {{4{ARG2S}}, codeOp[0], arg2S_t, arg1S, destS}; codeOp[1] = ARG2S; instrJR = instr[7]; jr = DoJR

  // Notes on the sheet:
  //   clk: Hz: 10
  //   MM Control Unit
  //   Console
  //   MM DataPath
  //   Memory access
  //   Control Unit State
  //   Flags
  //   DataPath registers
  //   RegA & RegB
  //   Clock counter
  //   RAM
  //   contents of eepromdualport_1 (hex, n*v repeats v):
  //   44,b,9f
endmodule
