// Digital circuit ALU.dig as structural Verilog
module ALU (
  input  [7:0] Arg1,
  input  [7:0] Arg2,
  input  Arg2S,
  input  [3:0] codeOp,
  output [7:0] out,
  output [2:0] Flags
);

  wire add_1_c_o, sub_1_c_o;
  wire [7:0] add_1_s, and_1_out, or_1_out, sub_1_s, xor_1_out, xor_2_out;

  Add #(.Bits(8)) add_1 (.a(Arg1), .b(Arg2), .c_i(1'b0), .s(add_1_s), .c_o(add_1_c_o));
  Sub #(.Bits(8)) sub_1 (.a(Arg1), .b(Arg2), .c_i(1'b0), .s(sub_1_s), .c_o(sub_1_c_o));
  assign and_1_out = Arg1 & Arg2;  // And and_1, 8 bits wide
  assign or_1_out = Arg1 | Arg2;  // Or or_1, 8 bits wide
  assign xor_1_out = Arg1 ^ Arg2;  // XOr xor_1, 8 bits wide
  assign xor_2_out = Arg1 ^ {8{Arg2S}};  // XOr xor_2, 8 bits wide
  Multiplexer #(.Selector_Bits(4), .Bits(8)) multiplexer_1 (
    .sel(codeOp), .in_0(add_1_s), .in_1(sub_1_s), .in_2(and_1_out), .in_3(or_1_out), .in_4(xor_1_out),
    .in_5({1'b0, Arg1[7:1]}), .in_6(sub_1_s), .in_7({8{1'b0}}), .in_8(xor_2_out), .in_9(Arg2),
    .in_10({8{1'b0}}), .in_11({8{1'b0}}), .in_12({8{1'b0}}), .in_13({8{1'b0}}), .in_14({8{1'b0}}),
    .in_15({8{1'b0}}), .out({Flags[2], out[6:0]}));
  Multiplexer #(.Selector_Bits(4)) multiplexer_2 (
    .sel(codeOp), .in_0(add_1_c_o), .in_1(sub_1_c_o), .in_2(1'b0), .in_3(1'b0), .in_4(1'b0), .in_5(Arg1[0]),
    .in_6(sub_1_c_o), .in_7(1'b0), .in_8(1'b0), .in_9(1'b0), .in_10(1'b0), .in_11(1'b0), .in_12(1'b0),
    .in_13(1'b0), .in_14(1'b0), .in_15(1'b0), .out(Flags[1]));
  nor nor_1 (Flags[0], out[0], out[1], out[2], out[3], out[4], out[5], out[6], Flags[2]);

  assign out[7] = Flags[2];
endmodule
