// Digital circuit MicroMachine.dig as structural Verilog
module MicroMachine (
  input  init,
  input  clk
);

  wire _1WordInstr, alu_1_p6, and_1_out, and_2_out, and_3_out, and_4_out, and_5_out, and_6_out, and_7_out,
       and_8_out, and_9_out, and_10_out, and_11_out, and_12_out, and_13_out, and_14_out, and_15_out, arg1S,
       arg2S, ceCst, ceFlags, ceInstr, ceM, cePC, ceRegA, ceRegB, destS, DoJA, doRETI, IncrPC, instrADD,
       instrALU, instrAND, instrCMP, InstrDecode, instrJA, instrLSR, instrMemRead, instrMemWrite, instrOR,
       instrPASS1, instrPASS2, instrSUB, instrXOR, IntAck, IRQ, jr, JRCondFalse, JumpCondTrue, memInstr,
       multiplexer_4_out, NoRegWrite, not_1_out, or_2_out, or_4_out, or_5_out, or_6_out, or_7_out, or_8_out,
       or_9_out, or_10_out, or_14_out, PC_p1, progFetch, RegWrite, RETI, SavedPC, SIGNAL_out;
  wire [2:0] multiplexer_9_out, SavedZCN, ZCN;
  wire [3:0] codeOp, counter_1_out, counter_1_out_2;
  wire [7:0] add_1_s, alu_1_p5, CST, MA, MDI, MDO, multiplexer_2_out, multiplexer_3_out, multiplexer_7_out,
       multiplexer_10_out, PC, Reg_A, Reg_B, undriven;
  wire [7:7] instr;

  not not_1 (not_1_out, instr[7]);
  Demultiplexer #(.Selector_Bits(4)) demultiplexer_1 (
    .sel(codeOp), .in(not_1_out), .out_0(instrADD), .out_1(instrSUB), .out_2(instrAND), .out_3(instrOR),
    .out_4(instrXOR), .out_5(instrLSR), .out_6(instrCMP), .out_8(instrPASS1), .out_9(instrPASS2),
    .out_13(instrMemRead), .out_14(instrMemWrite), .out_15(instrJA));  // open: out_7, out_10, out_11, out_12
  or or_1 (instrALU, instrADD, instrSUB, instrAND, instrOR, instrXOR, instrLSR, instrCMP, instrPASS1, instrPASS2);
  or or_2 (or_2_out, instrALU, instrMemRead, instrMemWrite);
  Multiplexer #(.Selector_Bits(2)) multiplexer_1 (
    .sel(codeOp[3:2]), .in_0(1'b1), .in_1(ZCN[0]), .in_2(ZCN[1]), .in_3(ZCN[2]), .out(JumpCondTrue));
  and and_1 (and_1_out, or_2_out, ~arg2S);  // And
  or or_3 (_1WordInstr, instrPASS1, instr[7], and_1_out);
  or or_4 (or_4_out, RegWrite, NoRegWrite, DoJA, RegWrite, jr, JRCondFalse, ceM, memInstr);
  or or_5 (or_5_out, RegWrite, NoRegWrite, DoJA, RegWrite, IntAck, jr, JRCondFalse, ceM, memInstr);
  and and_2 (and_2_out, InstrDecode, ~_1WordInstr);  // And
  and and_3 (and_3_out, ceCst, instrJA);
  and and_4 (and_4_out, InstrDecode, _1WordInstr, instrALU, ~instrCMP);  // And
  and and_5 (and_5_out, ceCst, instrALU, ~instrCMP);  // And
  and and_6 (and_6_out, InstrDecode, _1WordInstr, instrCMP);
  and and_7 (and_7_out, ceCst, instrCMP);
  and and_8 (and_8_out, InstrDecode, instr[7], JumpCondTrue);
  and and_9 (and_9_out, InstrDecode, instr[7], ~JumpCondTrue);  // And
  and and_10 (and_10_out, InstrDecode, _1WordInstr, instrMemRead);
  and and_11 (and_11_out, ceCst, instrMemRead);
  and and_12 (and_12_out, InstrDecode, _1WordInstr, instrMemWrite);
  and and_13 (and_13_out, ceCst, instrMemWrite);
  and and_14 (and_14_out, or_5_out, ~IRQ);  // And
  or or_6 (or_6_out, and_4_out, and_5_out);
  or or_7 (or_7_out, and_6_out, and_7_out);
  or or_8 (or_8_out, and_10_out, and_11_out);
  or or_9 (or_9_out, and_12_out, and_13_out);
  and and_15 (and_15_out, IRQ, or_4_out);
  D_FF_AS InstrFetch (.Set(init), .D(and_14_out), .C(clk), .Clr(1'b0), .Q(ceInstr));  // open: nQ
  D_FF_AS u_InstrDecode (.Set(1'b0), .D(ceInstr), .C(clk), .Clr(init), .Q(InstrDecode));  // open: nQ
  D_FF_AS u_IncrPC (.Set(1'b0), .D(and_2_out), .C(clk), .Clr(init), .Q(IncrPC));  // open: nQ
  D_FF_AS CstFetch (.Set(1'b0), .D(IncrPC), .C(clk), .Clr(init), .Q(ceCst));  // open: nQ
  D_FF_AS u_DoJA (.Set(1'b0), .D(and_3_out), .C(clk), .Clr(init), .Q(DoJA));  // open: nQ
  D_FF_AS u_RegWrite (.Set(1'b0), .D(or_6_out), .C(clk), .Clr(init), .Q(RegWrite));  // open: nQ
  D_FF_AS u_NoRegWrite (.Set(1'b0), .D(or_7_out), .C(clk), .Clr(init), .Q(NoRegWrite));  // open: nQ
  D_FF_AS JRCondTrue (.Set(1'b0), .D(and_8_out), .C(clk), .Clr(init), .Q(jr));  // open: nQ
  D_FF_AS u_JRCondFalse (.Set(1'b0), .D(and_9_out), .C(clk), .Clr(init), .Q(JRCondFalse));  // open: nQ
  D_FF_AS MemRead (.Set(1'b0), .D(or_8_out), .C(clk), .Clr(init), .Q(memInstr));  // open: nQ
  D_FF_AS MemWrite (.Set(1'b0), .D(or_9_out), .C(clk), .Clr(init), .Q(ceM));  // open: nQ
  D_FF_AS JumpToISR (.Set(1'b0), .D(and_15_out), .C(clk), .Clr(init), .Q(IntAck));  // open: nQ
  D_FF_AS u_doRETI (.Set(1'b0), .C(clk), .Clr(init), .Q(doRETI));  // open: D, nQ
  or or_10 (or_10_out, RegWrite, memInstr);
  or or_11 (cePC, RegWrite, NoRegWrite, DoJA, IncrPC, doRETI, jr, JRCondFalse, ceM, memInstr);
  or or_12 (ceFlags, RegWrite, doRETI, NoRegWrite);
  or or_13 (progFetch, ceInstr, ceCst);
  and and_16 (ceRegA, ~destS, or_10_out);  // And
  and and_17 (ceRegB, destS, or_10_out);
  // Reg RegIR: pin names not known; wires that end beside it: MDI, ceInstr, init, clk, {instr[7], codeOp, arg2S, arg1S, destS}
  Multiplexer #(.Bits(8)) multiplexer_2 (
    .sel(jr), .in_0(8'h1), .in_1({{4{codeOp[1]}}, codeOp[0], arg2S, arg1S, destS}), .out(multiplexer_2_out));
  Seven_Seg_Hex seven_seg_hex_1 (.d(MA[7:4]), .dp(1'b1));
  LED led_1 (.in(ceInstr));
  Seven_Seg_Hex seven_seg_hex_2 (.d(MA[3:0]), .dp(1'b1));
  LED led_2 (.in(InstrDecode));
  LED led_3 (.in(IncrPC));
  // Reg RegCst: pin names not known; wires that end beside it: MDI, ceCst, init, clk, CST
  Add #(.Bits(8)) add_1 (.a(multiplexer_2_out), .b(undriven), .c_i(1'b0), .s(add_1_s));  // open: c_o
  LED led_4 (.in(ceCst));
  LED led_5 (.in(DoJA));
  Seven_Seg_Hex seven_seg_hex_3 (.d(MDO[7:4]), .dp(1'b1));
  LED led_6 (.in(RegWrite));
  LED led_7 (.in(NoRegWrite));
  Multiplexer #(.Bits(8)) multiplexer_3 (.sel(DoJA), .in_0(add_1_s), .in_1(CST), .out(multiplexer_3_out));
  Seven_Seg_Hex seven_seg_hex_4 (.d(MDO[3:0]), .dp(1'b1));
  LED led_8 (.in(jr));
  LED led_9 (.in(JRCondFalse));
  Multiplexer multiplexer_4 (.in_0(1'b0), .in_1(multiplexer_3_out[0]), .out(multiplexer_4_out));  // open: sel
  // Reg SavedPC: pin names not known; wires that end beside it: PC, IntAck, 1'b0, clk, SavedPC
  Seven_Seg_Hex seven_seg_hex_5 (.d(MDI[7:4]), .dp(1'b1));
  LED led_10 (.in(memInstr));
  LED led_11 (.in(ceM));
  // Reg PC: pin names not known; wires that end beside it: PC_p1, cePC, init, clk, PC
  Multiplexer multiplexer_5 (.sel(RETI), .in_0(multiplexer_4_out), .in_1(SavedPC), .out(PC_p1));
  Seven_Seg_Hex seven_seg_hex_6 (.d(MDI[3:0]), .dp(1'b1));
  Seven_Seg_Hex seven_seg_hex_7 (.d(PC[7:4]), .dp(1'b1));
  Seven_Seg_Hex seven_seg_hex_8 (.d(PC[3:0]), .dp(1'b1));
  LED N (.in(ZCN[0]));
  LED C (.in(ZCN[1]));
  LED N_2 (.in(ZCN[2]));
  Multiplexer #(.Bits(8)) multiplexer_6 (.sel(arg1S), .in_0(Reg_A), .in_1(Reg_B), .out(MDO));
  Multiplexer #(.Bits(8)) multiplexer_7 (.sel(arg2S), .in_0(Reg_A), .in_1(CST), .out(multiplexer_7_out));
  Seven_Seg_Hex seven_seg_hex_9 (.d({instr[7], codeOp[3:1]}), .dp(1'b1));
  // ALU alu_1: pin names not known; wires that end beside it: MDO, multiplexer_7_out, arg2S, codeOp, alu_1_p5, alu_1_p6
  Seven_Seg_Hex seven_seg_hex_10 (.d({codeOp[0], arg2S, arg1S, destS}), .dp(1'b1));
  Multiplexer #(.Bits(8)) multiplexer_8 (.sel(progFetch), .in_0(multiplexer_7_out), .in_1(undriven), .out(MA));
  Seven_Seg_Hex seven_seg_hex_11 (.d(CST[7:4]), .dp(1'b1));
  Button SIGNAL (.out(SIGNAL_out));
  or or_14 (or_14_out, init, IntAck);
  Multiplexer multiplexer_9 (.sel(RETI), .in_0(alu_1_p6), .in_1(SavedZCN[0]), .out(multiplexer_9_out[0]));
  Seven_Seg_Hex seven_seg_hex_12 (.d(CST[3:0]), .dp(1'b1));
  RS_FF_AS rs_ff_as_1 (.S(SIGNAL_out), .R(or_14_out), .Q(IRQ));  // open: nQ
  Multiplexer #(.Bits(8)) multiplexer_10 (.sel(memInstr), .in_0(alu_1_p5), .in_1(MDI), .out(multiplexer_10_out));
  Register #(.Bits(3)) RegFlags (.D(multiplexer_9_out), .C(clk), .en(ceFlags), .Q(ZCN));
  Seven_Seg_Hex seven_seg_hex_13 (.d(Reg_A[7:4]), .dp(1'b1));
  LED u_IRQ (.in(IRQ));
  LED ACK (.in(IntAck));
  // Reg Reg_A: pin names not known; wires that end beside it: multiplexer_10_out, ceRegA, init, clk, Reg_A
  // Reg Reg_B: pin names not known; wires that end beside it: multiplexer_10_out, ceRegB, init, clk, Reg_B
  Register #(.Bits(3)) SavedRegFlags (.D(ZCN), .C(clk), .en(IntAck), .Q(SavedZCN));
  Seven_Seg_Hex seven_seg_hex_14 (.d(Reg_A[3:0]), .dp(1'b1));
  Seven_Seg_Hex seven_seg_hex_15 (.d(Reg_B[7:4]), .dp(1'b1));
  Seven_Seg_Hex seven_seg_hex_16 (.d(Reg_B[3:0]), .dp(1'b1));
  Seven_Seg_Hex seven_seg_hex_17 (.d(counter_1_out_2), .dp(1'b1));
  Seven_Seg_Hex seven_seg_hex_18 (.d(counter_1_out), .dp(1'b1));
  Counter #(.Bits(8)) counter_1 (.en(1'b1), .C(clk), .clr(init), .out({counter_1_out_2, counter_1_out}));  // open: ovf
  EEPROMDualPort #(.AddrBits(8), .Bits(8)) eepromdualport_1 (.A(MA), .Din(MDO), .str(ceM), .C(clk), .ld(1'b1), .D(MDI));
  // Pins of 1 and 3 bits meet at multiplexer_9_out
  // Pins of 1 and 8 bits meet at multiplexer_3_out
  // Pins of 1 and 8 bits meet at 8'ha0
  // Pins of 1 and 3 bits meet at SavedZCN
  // also tied to VCC on the sheet: IntAck

  // Other names for the same wires on the sheet: CstFetch = ceCst; InstrFetch = ceInstr; MemWrite = ceM;
  //   LoadRegs = doRETI; instr[6:0] = {codeOp, arg2S, arg1S, destS};
  //   offset[7:0] = {{4{codeOp[1]}}, codeOp[0], arg2S, arg1S, destS}; instrJR = instr[7]; ja = DoJA; JRCondTrue = jr;
  //   MemRead = memInstr; JumpToISR = IntAck; SaveRegs = IntAck

  // Notes on the sheet:
  //   MM Control Unit
  //   Interrupt signals (modifications needed!)
  //   Console
  //   MM DataPath
  //   Memory access
  //   Control Unit State
  //   Flags
  //   DataPath registers
  //   Interrupt management
  //   RegA & RegB
  //   Clock counter
  //   RAM
endmodule
