// Digital circuit add1bit.dig as structural Verilog
module add1bit (
  input  a,
  input  b,
  input  c_in,
  output s,
  output c_out
);

  wire and_1_out, and_2_out, and_3_out, xor_1_out;

  xor xor_1 (xor_1_out, b, a);
  and and_1 (and_1_out, c_in, b);
  and and_2 (and_2_out, c_in, a);
  and and_3 (and_3_out, b, a);
  xor xor_2 (s, c_in, xor_1_out);
  or or_1 (c_out, and_1_out, and_2_out, and_3_out);
endmodule
