// Digital circuit alu4bits.dig as structural Verilog
module alu4bits (
  input  [3:0] a,
  input  [3:0] b,
  input  [3:0] codeOp,
  output [3:0] s,
  output C,
  output Z,
  output N
);

  wire add4bit_1_c_out, lsr4bits_1_bit_out, sub4bits_1_c_out;
  wire [3:0] add4bit_1_s, and4bits_1_s, lsr4bits_1_s, not4bit_1_s, or4bits_1_s, sub4bits_1_s, xor4bits_1_s;

  add4bit add4bit_1 (.c_in(1'b0), .a(a), .b(b), .s(add4bit_1_s), .c_out(add4bit_1_c_out));
  sub4bits sub4bits_1 (.a(a), .b(b), .s(sub4bits_1_s), .c_out(sub4bits_1_c_out));
  and4bits and4bits_1 (.a(a), .b(b), .s(and4bits_1_s));
  or4bits or4bits_1 (.a(a), .b(b), .s(or4bits_1_s));
  xor4bits xor4bits_1 (.a(a), .b(b), .s(xor4bits_1_s));
  lsr4bits lsr4bits_1 (.a(a), .s(lsr4bits_1_s), .bit_out(lsr4bits_1_bit_out));
  not4bit not4bit_1 (.a(a), .s(not4bit_1_s));
  Multiplexer #(.Selector_Bits(4)) multiplexer_1 (
    .sel(codeOp), .in_0(add4bit_1_c_out), .in_1(sub4bits_1_c_out), .in_2(1'b0), .in_3(1'b0), .in_4(1'b0),
    .in_5(lsr4bits_1_bit_out), .in_6(1'b0), .in_7(1'b0), .in_8(1'b0), .in_9(1'b0), .in_10(1'b0),
    .in_11(1'b0), .in_12(1'b0), .in_13(1'b0), .in_14(1'b0), .in_15(1'b0), .out(C));
  Multiplexer #(.Bits(4), .Selector_Bits(4)) multiplexer_2 (
    .sel(codeOp), .in_0(add4bit_1_s), .in_1(sub4bits_1_s), .in_2(and4bits_1_s), .in_3(or4bits_1_s),
    .in_4(xor4bits_1_s), .in_5(lsr4bits_1_s), .in_6(not4bit_1_s), .in_7(b), .in_8(4'b0000), .in_9(4'b0000),
    .in_10(4'b0000), .in_11(4'b0000), .in_12(4'b0000), .in_13(4'b0000), .in_14(4'b0000), .in_15(4'b0000),
    .out({s[3:1], N}));
  nor nor_1 (Z, N, s[1], s[2], s[3]);

  assign s[0] = N;
endmodule
