// Digital circuit sub4bits.dig as structural Verilog
module sub4bits (
  input  [3:0] a,
  input  [3:0] b,
  output [3:0] s,
  output c_out
);

  wire [3:0] not4bit_1_s;

  not4bit not4bit_1 (.a(b), .s(not4bit_1_s));
  add4bit add4bit_1 (.c_in(1'b1), .a(a), .b(not4bit_1_s), .s(s), .c_out(c_out));
endmodule
