// Digital circuit add4bits.dig as structural Verilog
module add4bits (
  input  [3:0] b,
  input  c_in,
  input  [3:0] a,
  output c_out,
  output [3:0] s
);

  wire add1bit_1_c_out, add1bit_2_c_out, add1bit_3_c_out;

  add1bit add1bit_1 (.a(a[0]), .b(b[0]), .c_in(c_in), .s(s[0]), .c_out(add1bit_1_c_out));
  add1bit add1bit_2 (.a(a[1]), .b(b[1]), .c_in(add1bit_1_c_out), .s(s[1]), .c_out(add1bit_2_c_out));
  add1bit add1bit_3 (.a(a[2]), .b(b[2]), .c_in(add1bit_2_c_out), .s(s[2]), .c_out(add1bit_3_c_out));
  add1bit add1bit_4 (.a(a[3]), .b(b[3]), .c_in(add1bit_3_c_out), .s(s[3]), .c_out(c_out));
endmodule
