// Digital circuit add8bits.dig as structural Verilog
module add8bits (
  input  [7:0] a,
  input  [7:0] b,
  input  c_in,
  output c_out,
  output [7:0] s
);

  wire add4bits_1_c_out;

  add4bits add4bits_1 (.b(b[3:0]), .c_in(c_in), .a(a[3:0]), .c_out(add4bits_1_c_out), .s(s[3:0]));
  add4bits add4bits_2 (.b(b[7:4]), .c_in(add4bits_1_c_out), .a(a[7:4]), .c_out(c_out), .s(s[7:4]));
endmodule
