// Digital circuit alu.dig as structural Verilog
module alu (
  input  [3:0] a,
  input  [3:0] b,
  input  [3:0] op,
  output [3:0] C
);

  wire [3:0] add4bits_1_p4, lsr4bits_1_p3, sub4bits_1_s;
  wire [3:1] undriven, undriven_2, undriven_3, undriven_4, undriven_5, undriven_6, undriven_7, undriven_8,
       undriven_9, undriven_10, undriven_11, undriven_12, undriven_13;

  // add4bits add4bits_1: pin names not known; wires that end beside it: b, 1'b1, a, add4bits_1_p4
  sub4bits sub4bits_1 (.a(b), .b(a), .s(sub4bits_1_s));  // open: c_out
  and4bits and4bits_1 (.a(a), .b(b));  // open: s
  or4bits or4bits_1 (.a(a), .b(b));  // open: s
  xor4bits xor4bits_1 (.a(a), .b(b));  // open: s
  // lsr4bits lsr4bits_1: pin names not known; wires that end beside it: b, a, lsr4bits_1_p3
  not4bits not4bits_1 (.a(a));  // open: s
  Multiplexer #(.Bits(4), .Selector_Bits(4)) multiplexer_1 (
    .sel(op), .in_0(add4bits_1_p4), .in_1(sub4bits_1_s), .in_2({undriven_13, 1'b0}),
    .in_3({undriven_12, 1'b0}), .in_4({undriven_11, 1'b0}), .in_5(lsr4bits_1_p3), .in_6({undriven_10, 1'b0}),
    .in_7({undriven_9, 1'b0}), .in_8({undriven_8, 1'b0}), .in_9({undriven_7, 1'b0}),
    .in_10({undriven_6, 1'b0}), .in_11({undriven_5, 1'b0}), .in_12({undriven_4, 1'b0}),
    .in_13({undriven_3, 1'b0}), .in_14({undriven_2, 1'b0}), .in_15({undriven, 1'b0}), .out(C));
  // Pins of 1 and 4 bits meet at {undriven_13, 1'b0}
  // Pins of 1 and 4 bits meet at {undriven_12, 1'b0}
  // Pins of 1 and 4 bits meet at {undriven_11, 1'b0}
  // Pins of 1 and 4 bits meet at {undriven_10, 1'b0}
  // Pins of 1 and 4 bits meet at {undriven_9, 1'b0}
  // Pins of 1 and 4 bits meet at {undriven_8, 1'b0}
  // Pins of 1 and 4 bits meet at {undriven_7, 1'b0}
  // Pins of 1 and 4 bits meet at {undriven_6, 1'b0}
  // Pins of 1 and 4 bits meet at {undriven_5, 1'b0}
  // Pins of 1 and 4 bits meet at {undriven_4, 1'b0}
  // Pins of 1 and 4 bits meet at {undriven_3, 1'b0}
  // Pins of 1 and 4 bits meet at {undriven_2, 1'b0}
endmodule
