// Digital circuit and4bits.dig as structural Verilog
module and4bits (
  input  [3:0] a,
  input  [3:0] b,
  output [3:0] s
);

  and and_1 (s[0], a[0], b[0]);
  and and_2 (s[1], a[1], b[1]);
  and and_3 (s[2], a[2], b[2]);
  and and_4 (s[3], a[3], b[3]);
endmodule
