// Digital circuit and8bits.dig as structural Verilog
module and8bits (
  input  [7:0] a,
  input  [7:0] b,
  output [7:0] s
);

  and4bits and4bits_1 (.a(a[3:0]), .b(b[3:0]), .s(s[3:0]));
  and4bits and4bits_2 (.a(a[7:4]), .b(b[7:4]), .s(s[7:4]));
endmodule
