// Digital circuit not4bits.dig as structural Verilog
module not4bits (
  input  [3:0] a,
  output [3:0] s
);

  not not_1 (s[0], a[0]);
  not not_2 (s[1], a[1]);
  not not_3 (s[2], a[2]);
  not not_4 (s[3], a[3]);
endmodule
