// Digital circuit not8bits.dig as structural Verilog
module not8bits (
  input  [7:0] a,
  output [7:0] s
);

  not4bits not4bits_1 (.a(a[3:0]), .s(s[3:0]));
  not4bits not4bits_2 (.a(a[7:4]), .s(s[7:4]));
endmodule
