// Digital circuit sub4bits.dig as structural Verilog
module sub4bits (
  input  [3:0] b,
  input  [3:0] a,
  output c_out,
  output [3:0] s
);

  wire [3:0] not4bits_1_s;

  not4bits not4bits_1 (.a(b), .s(not4bits_1_s));
  add4bits add4bits_1 (.b(not4bits_1_s), .c_in(1'b1), .a(a), .c_out(c_out), .s(s));
endmodule
