// Digital circuit FlipFlop-RS.dig as structural Verilog
module FlipFlop_RS (
  input  D,
  input  RESET,
  input  CLK,
  input  EN,
  input  SET,
  output Q
);

  wire and_1_out, multiplexer_1_out, multiplexer_2_out, multiplexer_3_out, or_1_out;

  Multiplexer multiplexer_1 (.sel(EN), .in_0(Q), .in_1(D), .out(multiplexer_1_out));
  and and_1 (and_1_out, ~RESET, SET);  // And
  Multiplexer multiplexer_2 (.sel(or_1_out), .in_0(multiplexer_1_out), .in_1(and_1_out), .out(multiplexer_2_out));
  or or_1 (or_1_out, RESET, SET);
  Multiplexer multiplexer_3 (.sel(CLK), .in_0(multiplexer_2_out), .in_1(multiplexer_3_out), .out(multiplexer_3_out));
  Multiplexer multiplexer_4 (.sel(CLK), .in_0(Q), .in_1(multiplexer_3_out), .out(Q));
endmodule
