// Digital circuit add-n-times.dig as structural Verilog
module add_n_times (
  input  [3:0] a,
  input  [3:0] its
);

  wire nand_1_out;

  nand nand_1 (nand_1_out, its[0], 1'b0);
  add4bit add4bit_1 (.c_in(1'b0), .A(a), .B(a));  // open: s, c_out
  Demultiplexer demultiplexer_1 (.sel(nand_1_out), .in(nand_1_out));  // open: out_0, out_1
  // Pins of 1 and 4 bits meet at its
  // Pins of 1 and 4 bits meet at 4'b0000
endmodule
