// Digital circuit add1bit2.dig as structural Verilog
module add1bit2 (
  input  a,
  input  b,
  input  c_in,
  output s,
  output c_out
);

  wire and_1_out, and_2_out, and_3_out, or_1_out, xor_1_out;

  xor xor_1 (xor_1_out, a, b);
  xor xor_2 (s, xor_1_out, c_in);
  and and_1 (and_1_out, a, b);
  and and_2 (and_2_out, a, c_in);
  and and_3 (and_3_out, c_in, b);
  or or_1 (or_1_out, and_1_out, and_2_out);
  or or_2 (c_out, or_1_out, and_3_out);
endmodule
