// Digital circuit add1bitClean.dig as structural Verilog
module add1bitClean (
  input  a,
  input  b,
  input  c_in,
  output s,
  output c_out
);

  wire and_1_out, and_2_out, and_3_out, xor_1_out;

  xor xor_1 (xor_1_out, a, a);
  xor xor_2 (s, xor_1_out, a);
  and and_1 (and_1_out, a, a);
  and and_2 (and_2_out, a, a);
  and and_3 (and_3_out, a, a);
  or or_1 (c_out, and_1_out, and_2_out, and_3_out);

  assign b = a;
  assign c_in = a;
endmodule
