// Digital circuit add4bit.dig as structural Verilog
module add4bit (
  input  c_in,
  input  [3:0] A,
  input  [3:0] B,
  output [3:0] s,
  output c_out
);

  wire add1bit_1_c_out, add1bit_2_c_out, add1bit_3_c_out;

  add1bit add1bit_1 (.a(A[0]), .b(B[0]), .c_in(c_in), .s(s[0]), .c_out(add1bit_1_c_out));
  add1bit add1bit_2 (.a(A[1]), .b(B[1]), .c_in(add1bit_1_c_out), .s(s[1]), .c_out(add1bit_2_c_out));
  add1bit add1bit_3 (.a(A[2]), .b(B[2]), .c_in(add1bit_2_c_out), .s(s[2]), .c_out(add1bit_3_c_out));
  add1bit add1bit_4 (.a(A[3]), .b(B[3]), .c_in(add1bit_3_c_out), .s(s[3]), .c_out(c_out));
endmodule
