// Digital circuit add4bitClean.dig as structural Verilog
module add4bitClean (
  input  [3:0] a,
  input  b,
  input  c_in
);

  // add44bit add44bit_1: pin names not known; wires that end beside it: a
endmodule
