// Digital circuit alu.dig as structural Verilog
module alu (
  input  [3:0] a,
  input  [3:0] b,
  input  [3:0] op,
  output [3:0] s,
  output C,
  output Z,
  output N
);

  wire add_c_out, lsr_1_c_out, soustracteur_1_c_out;
  wire [3:0] add_s, and_1_s, lsr_1_s, not_1_s, or_1_s, soustracteur_1_s, xor_1_s;

  add4bit add (.c_in(1'b0), .A(a), .B(b), .s(add_s), .c_out(add_c_out));
  soustracteur soustracteur_1 (.a(a), .b(b), .s(soustracteur_1_s), .c_out(soustracteur_1_c_out));
  \and  and_1 (.a(a), .b(b), .s(and_1_s));
  \or  or_1 (.a(a), .b(b), .s(or_1_s));
  \xor  xor_1 (.a(a), .b(b), .s(xor_1_s));
  lsr lsr_1 (.a(a), .s(lsr_1_s), .c_out(lsr_1_c_out));
  \not  not_1 (.a(a), .s(not_1_s));
  Multiplexer #(.Selector_Bits(4)) multiplexer_1 (
    .sel(op), .in_0(add_c_out), .in_1(soustracteur_1_c_out), .in_2(1'b0), .in_3(1'b0), .in_4(1'b0),
    .in_5(lsr_1_c_out), .in_6(1'b0), .in_7(1'b0), .in_8(1'b0), .in_9(1'b0), .in_10(1'b0), .in_11(1'b0),
    .in_12(1'b0), .in_13(1'b0), .in_14(1'b0), .in_15(1'b0), .out(C));
  Multiplexer #(.Selector_Bits(4), .Bits(4)) multiplexer_2 (
    .sel(op), .in_0(add_s), .in_1(soustracteur_1_s), .in_2(and_1_s), .in_3(or_1_s), .in_4(xor_1_s),
    .in_5(lsr_1_s), .in_6(not_1_s), .in_7(b), .in_8(4'b0000), .in_9(4'b0000), .in_10(4'b0000),
    .in_11(4'b0000), .in_12(4'b0000), .in_13(4'b0000), .in_14(4'b0000), .in_15(4'b0000), .out({N, s[2:0]}));
  nor nor_1 (Z, s[0], s[1], s[2], N);

  assign s[3] = N;

  // Notes on the sheet:
  //   op: default 2
endmodule
