// Digital circuit chrono.dig as structural Verilog
module chrono (
  input  Clock
);

  wire and_1_out, and_2_out, and_3_out, and_4_out, and_5_out, and_6_out, and_7_out, and_8_out, and_9_out,
       and_10_out, and_11_out, and_12_out, Button, compte, or_1_out, or_2_out, or_3_out, or_4_out, or_5_out,
       or_6_out, q0, q1, q2, q3, q4, q5, reset, set;
  wire [3:0] Reg_q, Reg_q_2, Reg_q_3, Reg_q_4;
  wire [15:0] Add_s, multiplexer_1_out;

  Reset #(.invertOutput("false")) u_set (.out(set));
  and and_1 (and_1_out, q5, ~Button);  // And
  and and_2 (and_2_out, q0, ~Button);  // And
  and and_3 (and_3_out, q2, ~Button);  // And
  and and_4 (and_4_out, q1, ~Button);  // And
  and and_5 (and_5_out, q3, ~Button);  // And
  and and_6 (and_6_out, q4, ~Button);  // And
  or or_1 (or_1_out, and_1_out, and_2_out);
  or or_2 (or_2_out, and_3_out, and_4_out);
  or or_3 (or_3_out, and_5_out, and_6_out);
  D_FF_AS u_q0 (.Set(set), .D(or_1_out), .C(Clock), .Clr(1'b0), .Q(q0));  // open: nQ
  D_FF_AS u_q2 (.Set(1'b0), .D(or_2_out), .C(Clock), .Clr(set), .Q(q2));  // open: nQ
  D_FF_AS u_q4 (.Set(1'b0), .D(or_3_out), .C(Clock), .Clr(set), .Q(q4));  // open: nQ
  Button u_Button (.out(Button));
  and and_7 (and_7_out, q1, Button);
  and and_8 (and_8_out, q0, Button);
  and and_9 (and_9_out, q2, Button);
  and and_10 (and_10_out, q3, Button);
  and and_11 (and_11_out, q4, Button);
  and and_12 (and_12_out, q5, Button);
  or or_4 (or_4_out, and_11_out, and_12_out);
  Add #(.Bits(16)) Add (
    .a({Reg_q_4, Reg_q_3, Reg_q_2, Reg_q}), .b(multiplexer_1_out), .c_i(1'b0), .s(Add_s));  // open: c_o
  or or_5 (or_5_out, and_7_out, and_8_out);
  or or_6 (or_6_out, and_9_out, and_10_out);
  D_FF_AS #(.Bits(16)) Reg (
    .Set(1'b0), .D(Add_s), .C(Clock), .Clr(reset), .Q({Reg_q_4, Reg_q_3, Reg_q_2, Reg_q}));  // open: nQ
  Multiplexer #(.Bits(16)) multiplexer_1 (.sel(compte), .in_0({16{1'b0}}), .in_1(16'h1), .out(multiplexer_1_out));
  D_FF_AS u_q1 (.Set(1'b0), .D(or_5_out), .C(Clock), .Clr(set), .Q(q1));  // open: nQ
  D_FF_AS u_q3 (.Set(1'b0), .D(or_6_out), .C(Clock), .Clr(set), .Q(q3));  // open: nQ
  D_FF_AS u_q5 (.Set(1'b0), .D(or_4_out), .C(Clock), .Clr(set), .Q(q5));  // open: nQ
  or or_7 (compte, q1, q2);
  or or_8 (reset, q0, q5);
  Seven_Seg_Hex seven_seg_hex_1 (.d(Reg_q_4), .dp(1'b1));
  Seven_Seg_Hex seven_seg_hex_2 (.d(Reg_q_3), .dp(1'b1));
  Seven_Seg_Hex seven_seg_hex_3 (.d(Reg_q_2), .dp(1'b1));
  Seven_Seg_Hex seven_seg_hex_4 (.d(Reg_q), .dp(1'b1));

  // Notes on the sheet:
  //   Clock: Hz: 50
endmodule
