// Digital circuit clicgnotant-automate.dig as structural Verilog
module clicgnotant_automate (
  input  clock,
  input  CWD
);

  wire and_1_out, register_1_s;

  and and_1 (and_1_out, CWD, ~register_1_s);  // And
  register register_1 (.e1(and_1_out), .Ck(clock), .s(register_1_s));
  LED led_1 (.in(register_1_s));
endmodule
