// Digital circuit clignotant-log.dig as structural Verilog
module clignotant_log (
  input  clock,
  input  c
);

  wire and_1_out, and_2_out, and_3_out, and_4_out, and_5_out, and_6_out, and_7_out, and_8_out, and_9_out,
       or_1_out, or_2_out, or_3_out, or_4_out, or_5_out, reset_out, S0, S1;

  and and_1 (and_1_out, ~S0, ~S1, c);  // And
  and and_2 (and_2_out, ~S0, S1, c);  // And
  and and_3 (and_3_out, ~S0, S1, c);  // And
  and and_4 (and_4_out, S0, ~S1, c);  // And
  or or_1 (or_1_out, and_3_out, and_4_out);
  or or_2 (or_2_out, and_1_out, and_2_out);
  Reset #(.invertOutput("false")) reset (.out(reset_out));
  D_FF_AS d_ff_as_1 (.Set(1'b0), .D(or_2_out), .C(clock), .Clr(reset_out), .Q(S0));  // open: nQ
  D_FF_AS d_ff_as_2 (.Set(1'b0), .D(or_1_out), .C(clock), .Clr(reset_out), .Q(S1));  // open: nQ
  and and_5 (and_5_out, S0, ~S1);  // And
  and and_6 (and_6_out, S0, S1);
  and and_7 (and_7_out, S0, S1);
  and and_8 (and_8_out, ~S0, S1);  // And
  and and_9 (and_9_out, S0, S1);
  or or_3 (or_3_out, S0, S1);
  or or_4 (or_4_out, and_5_out, and_6_out);
  or or_5 (or_5_out, and_8_out, and_9_out);
  LED AVG (.in(or_4_out));
  LED ARG3 (.in(and_7_out));
  LED ARG2 (.in(or_5_out));
  LED ARG1 (.in(or_3_out));
endmodule
