// Digital circuit clignotants-gauche.dig as structural Verilog
module clignotants_gauche (
  input  clk,
  input  cg
);

  wire and_1_out, register_1_s;

  and and_1 (and_1_out, ~register_1_s, cg);  // And
  register register_1 (.e1(and_1_out), .Ck(clk), .s(register_1_s));
  LED gauche_avant (.in(register_1_s));
  LED gauche_arriere (.in(register_1_s));
endmodule
