// Digital circuit flil-flop-reset.dig as structural Verilog
module flil_flop_reset (
  input  e,
  input  clock,
  input  reset,
  output s
);

  wire multiplexer_1_out;

  Multiplexer multiplexer_1 (.sel(reset), .in_0(e), .in_1(1'b0), .out(multiplexer_1_out));
  register register_1 (.e1(multiplexer_1_out), .Ck(clock), .s(s));
endmodule
