// Digital circuit flip-flop-reset-enable.dig as structural Verilog
module flip_flop_reset_enable (
  input  e,
  input  reset,
  input  enable,
  input  clock,
  output s
);

  wire multiplexer_1_out, multiplexer_2_out;

  Multiplexer multiplexer_1 (.sel(enable), .in_0(s), .in_1(e), .out(multiplexer_1_out));
  Multiplexer multiplexer_2 (.sel(reset), .in_0(multiplexer_1_out), .in_1(1'b0), .out(multiplexer_2_out));
  register register_1 (.e1(multiplexer_2_out), .Ck(clock), .s(s));
endmodule
