// Digital circuit ford.dig as structural Verilog
module ford (
  input  Warnings,
  input  clock
);

  wire and_14_out, and_15_out, and_16_out, and_17_out, and_18_out, and_19_out, and_20_out, ARD1, ARD2, ARD3,
       ARG1, ARG2, ARG3, AVD, AVG, cd, CDcg, cdCG_t, cg, CG_plus_cd, cg_plus_CD_t, CGCD, Droite_out,
       Gauche_out, or_3_out, q0, q1, q1_CG_plus_cd, q2, q2_CG_plus_cd, q3, q3_CG_plus_cd, q3CDcg, q4, q5,
       q5_CG_plus_cd, q6, q6_CG_plus_cd, q7, q7_CG_plus_cd, q7cdCG, reset;

  and and_1 (q7cdCG, q7, cdCG_t);
  and and_2 (q3CDcg, q3, CDcg);
  and and_3 (CDcg, ~cd, cg);  // And
  and and_4 (cdCG_t, cd, ~cg);  // And
  and and_5 (CGCD, ~cg, ~cd);  // And
  or or_1 (CG_plus_cd, ~cg, cd);  // Or
  or or_2 (cg_plus_CD_t, cg, ~cd);  // Or
  and and_6 (q1_CG_plus_cd, q1, CG_plus_cd);
  and and_7 (q2_CG_plus_cd, q2, CG_plus_cd);
  and and_8 (q3_CG_plus_cd, q3, CG_plus_cd);
  and and_9 (q5_CG_plus_cd, q5, cg_plus_CD_t);
  and and_10 (q6_CG_plus_cd, q6, cg_plus_CD_t);
  and and_11 (q6_CG_plus_cd, q6, cg_plus_CD_t);
  and and_12 (q7_CG_plus_cd, q7, cg_plus_CD_t);
  and and_13 (q7_CG_plus_cd, q7, cg_plus_CD_t);
  Button Gauche (.out(Gauche_out));
  Button Droite (.out(Droite_out));
  Reset #(.invertOutput("false")) u_Reset (.out(reset));
  comodo comodo_1 (.G(Gauche_out), .D(Droite_out), .W(Warnings), .CG(cg), .CD(cd));
  or or_3 (or_3_out, q1_CG_plus_cd, q2_CG_plus_cd, q3_CG_plus_cd, q4, q3CDcg, q6_CG_plus_cd, q7_CG_plus_cd, CGCD, q5_CG_plus_cd, q7cdCG);
  and and_14 (and_14_out, q0, CDcg);
  and and_15 (and_15_out, q1, CDcg);
  and and_16 (and_16_out, q2, CDcg);
  D_FF_AS u_q0 (.Set(1'b0), .D(or_3_out), .C(clock), .Clr(reset), .Q(q0));  // open: nQ
  D_FF_AS u_q1 (.Set(1'b0), .D(and_14_out), .C(clock), .Clr(reset), .Q(q1));  // open: nQ
  D_FF_AS u_q2 (.Set(1'b0), .D(and_15_out), .C(clock), .Clr(reset), .Q(q2));  // open: nQ
  D_FF_AS u_q3 (.Set(1'b0), .D(and_16_out), .C(clock), .Clr(reset), .Q(q3));  // open: nQ
  LED u_ARG3 (.in(ARG3));
  LED u_AVG (.in(AVG));
  LED u_ARG1 (.in(ARG1));
  LED u_ARG2 (.in(ARG2));
  and and_17 (and_17_out, q0, cd, cg);
  and and_18 (and_18_out, q0, cdCG_t);
  and and_19 (and_19_out, q5, cdCG_t);
  and and_20 (and_20_out, q6, cdCG_t);
  D_FF_AS u_q4 (.Set(1'b0), .D(and_17_out), .C(clock), .Clr(reset), .Q(q4));  // open: nQ
  D_FF_AS u_q5 (.Set(1'b0), .D(and_18_out), .C(clock), .Clr(reset), .Q(q5));  // open: nQ
  D_FF_AS d_ff_as_1 (.Set(1'b0), .D(and_19_out), .C(clock), .Clr(reset), .Q(q6));  // open: nQ
  D_FF_AS d_ff_as_2 (.Set(1'b0), .D(and_20_out), .C(clock), .Clr(reset), .Q(q7));  // open: nQ
  LED u_AVD (.in(AVD));
  LED u_ARD1 (.in(ARD1));
  LED u_ARD2 (.in(ARD2));
  LED u_ARD3 (.in(ARD3));
  or or_4 (AVG, q1, q4, q3);
  or or_5 (ARG1, q4, q1, q2, q3);
  or or_6 (ARG2, q2, q4, q3);
  or or_7 (ARG3, q3, q4);
  or or_8 (AVD, q5, q4, q7);
  or or_9 (ARD1, q5, q6, q7, q4);
  or or_10 (ARD2, q6, q4, q7);
  or or_11 (ARD3, q7, q4);

  // Other names for the same wires on the sheet: clk = clock

  // Notes on the sheet:
  //   Raccourcis
endmodule
