// Digital circuit less-equal-result.dig as structural Verilog
module less_equal_result (
  input  [3:0] a,
  input  [3:0] b,
  output [3:0] s
);

  wire sign_bit;
  wire [2:0] soustracteur_1_s;

  soustracteur soustracteur_1 (.a(a), .b(b), .s({sign_bit, soustracteur_1_s}));  // open: c_out
  Multiplexer #(.Bits(4)) multiplexer_1 (.sel(sign_bit), .in_0(a), .in_1(b), .out(s));
endmodule
