// Digital circuit less-equal.dig as structural Verilog
module less_equal (
  input  [3:0] a,
  input  [3:0] b,
  output s
);

  wire [3:0] soustracteur_1_s;

  soustracteur soustracteur_1 (.a(a), .b(b), .s(soustracteur_1_s));  // open: c_out
  not not_1 (s, soustracteur_1_s[3]);
endmodule
