// Digital circuit memory.dig as structural Verilog
module memory (
  input  [3:0] data,
  input  WE,
  input  [1:0] addr,
  input  clock,
  input  reset,
  output [3:0] s
);

  wire demultiplexer_1_out_0, demultiplexer_1_out_1, demultiplexer_1_out_2, demultiplexer_1_out_3;
  wire [3:0] register4_1_s, register4_2_s, register4_3_s, register4_4_s;

  Demultiplexer #(.Selector_Bits(2)) demultiplexer_1 (
    .sel(addr), .in(WE), .out_0(demultiplexer_1_out_0), .out_1(demultiplexer_1_out_1),
    .out_2(demultiplexer_1_out_2), .out_3(demultiplexer_1_out_3));
  register4 register4_1 (.a(data), .reset(reset), .clock(clock), .enable(demultiplexer_1_out_0), .s(register4_1_s));
  register4 register4_2 (.a(data), .reset(reset), .clock(clock), .enable(demultiplexer_1_out_1), .s(register4_2_s));
  register4 register4_3 (.a(data), .reset(reset), .clock(clock), .enable(demultiplexer_1_out_2), .s(register4_3_s));
  register4 register4_4 (.a(data), .reset(reset), .clock(clock), .enable(demultiplexer_1_out_3), .s(register4_4_s));
  Multiplexer #(.Bits(4), .Selector_Bits(2)) multiplexer_1 (
    .sel(addr), .in_0(register4_1_s), .in_1(register4_2_s), .in_2(register4_3_s), .in_3(register4_4_s),
    .out(s));
endmodule
