// Digital circuit minuteur.dig as structural Verilog
module minuteur (
  input  [15:0] TIME_IN,
  input  START,
  input  STOP,
  input  SET,
  input  clk
);

  wire and_1_out, and_2_out, and_3_out, and_4_out, and_5_out, and_6_out, decompte, or_1_out, or_2_out,
       or_3_out, q0, q2, q3, set_t;
  wire [3:0] reg_q, reg_q_2, reg_q_3;
  wire [15:0] multiplexer_1_out;
  wire [15:12] reg_q_4;

  and and_1 (and_1_out, q2, STOP);
  and and_2 (and_2_out, ~SET, ~START);  // And
  or or_1 (or_1_out, and_1_out, and_2_out);
  and and_3 (and_3_out, decompte, STOP);
  D_FF_AS u_q0 (.Set(set_t), .D(or_1_out), .C(clk), .Clr(1'b0), .Q(q0));  // open: nQ
  D_FF_AS u_q3 (.Set(1'b0), .D(and_3_out), .C(clk), .Clr(set_t), .Q(q3));  // open: nQ
  Reset #(.invertOutput("false")) u_set (.out(set_t));
  and and_4 (and_4_out, q0, START);
  and and_5 (and_5_out, q3, START);
  and and_6 (and_6_out, ~1'b0, ~STOP);  // And
  D_FF_AS #(.Bits(16)) \reg  (
    .Set(1'b0), .D({reg_q_4, reg_q_3, reg_q_2, reg_q}), .C(clk), .Clr(1'b0),
    .Q({reg_q_4, reg_q_3, reg_q_2, reg_q}));  // open: nQ
  or or_2 (or_2_out, and_4_out, and_5_out, and_6_out);
  or or_3 (or_3_out, 1'b0, ~STOP);  // Or
  Sub #(.Bits(16)) sub_1 (
    .a(multiplexer_1_out), .b({reg_q_4, reg_q_3, reg_q_2, reg_q}), .c_i(1'b0),
    .s({reg_q_4, reg_q_3, reg_q_2, reg_q}));  // open: c_o
  Multiplexer #(.Bits(16)) multiplexer_1 (.sel(decompte), .in_0({16{1'b0}}), .in_1(16'h1), .out(multiplexer_1_out));
  D_FF_AS q1 (.Set(1'b0), .D(or_2_out), .C(clk), .Clr(set_t), .Q(decompte));  // open: nQ
  D_FF_AS u_q2 (.Set(1'b0), .D(or_3_out), .C(clk), .Clr(set_t), .Q(q2));  // open: nQ
  LED led_1 (.in(STOP));
  Seven_Seg_Hex seven_seg_hex_1 (.d(reg_q_4), .dp(1'b1));
  Seven_Seg_Hex seven_seg_hex_2 (.d(reg_q_3), .dp(1'b1));
  Seven_Seg_Hex seven_seg_hex_3 (.d(reg_q_2), .dp(1'b1));
  Seven_Seg_Hex seven_seg_hex_4 (.d(reg_q), .dp(1'b1));

  // Other names for the same wires on the sheet: DRING = STOP; q1 = decompte
endmodule
