// Digital circuit mul.dig as structural Verilog
module mul (
  input  a1,
  input  b1,
  input  a2,
  input  b2,
  input  c1,
  input  c2,
  output s
);

  wire and_1_out, and_2_out, and_3_out, and_4_out, and_5_out, and_6_out, or_1_out, or_2_out;

  and and_1 (and_1_out, c1, a1);
  and and_2 (and_2_out, ~c1, b1);  // And
  and and_3 (and_3_out, c1, a2);
  and and_4 (and_4_out, ~c1, b2);  // And
  or or_1 (or_1_out, and_1_out, and_2_out);
  or or_2 (or_2_out, and_3_out, and_4_out);
  and and_5 (and_5_out, or_1_out, c2);
  and and_6 (and_6_out, ~c2, or_2_out);  // And
  or or_3 (s, and_5_out, and_6_out);
endmodule
