// Digital circuit or.dig as structural Verilog
module \or  (
  input  [3:0] a,
  input  [3:0] b,
  output [3:0] s
);

  or or_1 (s[0], a[0], b[0]);
  or or_2 (s[1], a[1], b[1]);
  or or_3 (s[2], a[2], b[2]);
  or or_4 (s[3], a[3], b[3]);
endmodule
