// Digital circuit q27.dig as structural Verilog
module q27 (
  input  [3:0] A,
  input  [3:0] B,
  input  shift,
  input  CReset,
  input  clk,
  input  init,
  input  ADD
);

  wire Add_2_c_o, B0, carry, fini, or_1_out, r1_p7;
  wire [1:0] add_1_s, count, multiplexer_1_out;
  wire [3:0] r1_p1, r1data, r2data;

  Multiplexer #(.Bits(2)) multiplexer_1 (.sel(init), .in_0(2'b00), .in_1(add_1_s), .out(multiplexer_1_out));
  or or_1 (or_1_out, init, ADD);
  Register #(.Bits(2)) r_compteur (.D(multiplexer_1_out), .C(clk), .en(or_1_out), .Q(count));
  Add #(.Bits(2)) add_1 (.a(2'b01), .b(count), .c_i(1'b0), .s(add_1_s));  // open: c_o
  // registre_a_decalage_PIPO r1: pin names not known; wires that end beside it: r1_p1, carry, ADD, init, shift, clk, r1_p7, r1data
  Add #(.Bits(4)) Add_2 (.a(A), .b(r1data), .c_i(1'b0), .s(r1_p1), .c_o(Add_2_c_o));
  // Probe on r1data
  flip_flop_reset_enable flip_flop_reset_enable_1 (.e(Add_2_c_o), .reset(CReset), .enable(ADD), .clock(clk), .s(carry));
  // registre_a_decalage_PIPO r2: pin names not known; wires that end beside it: B, r1_p7, init, 1'b0, shift, clk, B0, r2data
  Seven_Seg_Hex seven_seg_hex_1 (.d({2'b00, count}), .dp(1'b1));
  // Probe on r2data
  and and_1 (fini, count[0], count[1]);
  Seven_Seg_Hex seven_seg_hex_2 (.d(r1data), .dp(1'b1));
  Seven_Seg_Hex seven_seg_hex_3 (.d(r2data), .dp(1'b1));

  // Notes on the sheet:
  //   A: default 7
  //   B: default 4
endmodule
