// Digital circuit register.dig as structural Verilog
module register (
  input  e1,
  input  Ck,
  output s
);

  wire multiplexer_1_out;

  Multiplexer multiplexer_1 (.sel(Ck), .in_0(e1), .in_1(multiplexer_1_out), .out(multiplexer_1_out));
  Multiplexer multiplexer_2 (.sel(Ck), .in_0(s), .in_1(multiplexer_1_out), .out(s));
endmodule
