// Digital circuit register4.dig as structural Verilog
module register4 (
  input  [3:0] a,
  input  reset,
  input  clock,
  input  enable,
  output [3:0] s
);

  flip_flop_reset_enable flip_flop_reset_enable_1 (.e(a[3]), .reset(reset), .enable(enable), .clock(clock), .s(s[3]));
  flip_flop_reset_enable flip_flop_reset_enable_2 (.e(a[2]), .reset(reset), .enable(enable), .clock(clock), .s(s[2]));
  flip_flop_reset_enable flip_flop_reset_enable_3 (.e(a[1]), .reset(reset), .enable(enable), .clock(clock), .s(s[1]));
  flip_flop_reset_enable flip_flop_reset_enable_4 (.e(a[0]), .reset(reset), .enable(enable), .clock(clock), .s(s[0]));
endmodule
