// Digital circuit registre-a-decalage-PIPO.dig as structural Verilog
module registre_a_decalage_PIPO (
  input  B_in,
  input  CLEAR,
  input  SHIFT,
  input  CLK,
  input  SET,
  input  [3:0] Data_in,
  output B_out,
  output [3:0] Data_out
);

  wire multiplexer_1_out, multiplexer_2_out, multiplexer_3_out, multiplexer_4_out, or_1_out;

  or or_1 (or_1_out, SET, SHIFT);
  Multiplexer multiplexer_1 (.sel(SET), .in_0(B_in), .in_1(Data_in[3]), .out(multiplexer_1_out));
  FlipFlop_RS flipflop_rs_1 (
    .D(multiplexer_1_out), .EN(or_1_out), .RESET(CLEAR), .SET(1'b0), .CLK(CLK), .Q(Data_out[3]));
  Multiplexer multiplexer_2 (.sel(SET), .in_0(Data_out[3]), .in_1(Data_in[2]), .out(multiplexer_2_out));
  FlipFlop_RS flipflop_rs_2 (
    .D(multiplexer_2_out), .EN(or_1_out), .RESET(CLEAR), .SET(1'b0), .CLK(CLK), .Q(Data_out[2]));
  Multiplexer multiplexer_3 (.sel(SET), .in_0(Data_out[2]), .in_1(Data_in[1]), .out(multiplexer_3_out));
  FlipFlop_RS flipflop_rs_3 (
    .D(multiplexer_3_out), .EN(or_1_out), .RESET(CLEAR), .SET(1'b0), .CLK(CLK), .Q(Data_out[1]));
  Multiplexer multiplexer_4 (.sel(SET), .in_0(Data_out[1]), .in_1(Data_in[0]), .out(multiplexer_4_out));
  FlipFlop_RS flipflop_rs_4 (.D(multiplexer_4_out), .EN(or_1_out), .RESET(CLEAR), .SET(1'b0), .CLK(CLK), .Q(B_out));

  assign Data_out[0] = B_out;
endmodule
