// Digital circuit shift-register.dig as structural Verilog
module shift_register (
  input  B_in,
  input  clk,
  input  shift,
  output b_out,
  output DATA_OUT
);

  wire register_2_q, register_3_q;

  Register register_1 (.D(B_in), .C(clk), .en(shift));  // open: Q
  Register register_2 (.C(clk), .en(shift), .Q(register_2_q));  // open: D
  Register register_3 (.D(register_2_q), .C(clk), .en(shift), .Q(register_3_q));
  Register register_4 (.D(register_3_q), .C(clk), .en(shift), .Q(b_out));
endmodule
