// Digital circuit soustracteur.dig as structural Verilog
module soustracteur (
  input  [3:0] a,
  input  [3:0] b,
  output [3:0] s,
  output c_out
);

  wire [3:0] not_1_s;

  \not  not_1 (.a(b), .s(not_1_s));
  add4bit add4bit_1 (.c_in(1'b1), .A(a), .B(not_1_s), .s(s), .c_out(c_out));
endmodule
