// Digital circuit soustracteur8bits.dig as structural Verilog
module soustracteur8bits (
  input  [7:0] a,
  input  [7:0] b,
  output [7:0] s
);

  soustracteur soustracteur_1 (.a(a[3:0]), .b(b[3:0]), .s(s[3:0]));  // open: c_out
  soustracteur soustracteur_2 (.a(a[7:4]), .b(b[7:4]), .s(s[7:4]));  // open: c_out
endmodule
