// Digital circuit test.dig as structural Verilog
module test (
  input  [31:0] a,
  input  [1:0] op,
  output [31:0] s
);

  wire [7:0] demultiplexer_1_out_0, demultiplexer_1_out_1, demultiplexer_1_out_2, demultiplexer_1_out_3,
       demultiplexer_2_out_0, demultiplexer_2_out_1, demultiplexer_2_out_2, demultiplexer_2_out_3,
       demultiplexer_3_out_0, demultiplexer_3_out_1, demultiplexer_3_out_2, demultiplexer_3_out_3,
       demultiplexer_4_out_0, demultiplexer_4_out_1, demultiplexer_4_out_2, demultiplexer_4_out_3;

  Demultiplexer #(.Bits(8), .Selector_Bits(2)) demultiplexer_1 (
    .sel(op), .in(a[7:0]), .out_0(demultiplexer_1_out_0), .out_1(demultiplexer_1_out_1),
    .out_2(demultiplexer_1_out_2), .out_3(demultiplexer_1_out_3));
  Demultiplexer #(.Selector_Bits(2), .Bits(8)) demultiplexer_2 (
    .sel(op), .in(a[15:8]), .out_0(demultiplexer_2_out_0), .out_1(demultiplexer_2_out_1),
    .out_2(demultiplexer_2_out_2), .out_3(demultiplexer_2_out_3));
  Demultiplexer #(.Selector_Bits(2), .Bits(8)) demultiplexer_3 (
    .sel(op), .in(a[23:16]), .out_0(demultiplexer_3_out_0), .out_1(demultiplexer_3_out_1),
    .out_2(demultiplexer_3_out_2), .out_3(demultiplexer_3_out_3));
  Demultiplexer #(.Selector_Bits(2), .Bits(8)) demultiplexer_4 (
    .sel(op), .in(a[31:24]), .out_0(demultiplexer_4_out_0), .out_1(demultiplexer_4_out_1),
    .out_2(demultiplexer_4_out_2), .out_3(demultiplexer_4_out_3));
  assign s[7:0] = demultiplexer_1_out_0 | demultiplexer_1_out_1 | demultiplexer_1_out_2 | demultiplexer_1_out_3;  // Or or_1, 8 bits wide
  assign s[15:8] = demultiplexer_2_out_0 | demultiplexer_2_out_1 | demultiplexer_2_out_2 | demultiplexer_2_out_3;  // Or or_2, 8 bits wide
  assign s[23:16] = demultiplexer_3_out_0 | demultiplexer_3_out_1 | demultiplexer_3_out_2 | demultiplexer_3_out_3;  // Or or_3, 8 bits wide
  assign s[31:24] = demultiplexer_4_out_0 | demultiplexer_4_out_1 | demultiplexer_4_out_2 | demultiplexer_4_out_3;  // Or or_4, 8 bits wide
endmodule
