// Digital circuit thunderbird-codage-log.dig as structural Verilog
module thunderbird_codage_log (
  input  CG
);

  // And and_1 is placed but not wired
  // And and_2 is placed but not wired
  // And and_3 is placed but not wired
  // And and_4 is placed but not wired
  register r0 ();  // open: e1, Ck, s
  register r1 ();  // open: e1, Ck, s
endmodule
