// Digital circuit thunderbird-one-hot-coding.dig as structural Verilog
module thunderbird_one_hot_coding (
  input  CG,
  input  clock
);

  wire and_1_out, and_2_out, and_3_out, or_1_out, or_2_out, or_3_out, or_4_out, q0_s, q1_s, q2_s, q3_s;

  or or_1 (or_1_out, ~CG, q3_s);  // Or
  and and_1 (and_1_out, CG, q0_s);
  and and_2 (and_2_out, CG, q1_s);
  and and_3 (and_3_out, CG, q2_s);
  register q0 (.e1(or_1_out), .Ck(clock), .s(q0_s));
  register q1 (.e1(and_1_out), .Ck(clock), .s(q1_s));
  register q2 (.e1(and_2_out), .Ck(clock), .s(q2_s));
  register q3 (.e1(and_3_out), .Ck(clock), .s(q3_s));
  or or_2 (or_2_out, q1_s, q3_s);
  or or_3 (or_3_out, q2_s, q3_s);
  or or_4 (or_4_out, q1_s, q2_s, q3_s);
  LED AG (.in(or_2_out));
  LED ARG1 (.in(q3_s));
  LED ARG2 (.in(or_3_out));
  LED ARG3 (.in(or_4_out));
endmodule
