// Digital circuit xor.dig as structural Verilog
module \xor  (
  input  [3:0] a,
  input  [3:0] b,
  output [3:0] s
);

  xor xor_1 (s[0], a[0], b[0]);
  xor xor_2 (s[1], a[1], b[1]);
  xor xor_3 (s[2], a[2], b[2]);
  xor xor_4 (s[3], a[3], b[3]);
endmodule
